# Fritzing sketch schema_capteur_DS18B20 (saved by Fritzing 0.9.2b)

parts:
  NRF24L1_Emetteur_2_4Ghz = NRF24L01
  R1 = Resistor [tolerance=±5% resistance=4.7k package=THT]
  Température_extérieur = DS18B20 1-Wire Temperature Sensor [part_number=DS18B20]
  Composant2 = Arduino Nano (Rev3.0)

nets:
  VCC: NRF24L1_Emetteur_2_4Ghz.VCC, Composant2.3V3
  N1: NRF24L1_Emetteur_2_4Ghz.CSN, Composant2.D10
  N2: NRF24L1_Emetteur_2_4Ghz.MOSI, Composant2.D11/MOSI
  N3: NRF24L1_Emetteur_2_4Ghz.IRQ, Composant2.D2
  GND: NRF24L1_Emetteur_2_4Ghz.GND, Composant2.GND
  N4: NRF24L1_Emetteur_2_4Ghz.CE, Composant2.D9
  N5: NRF24L1_Emetteur_2_4Ghz.SCK, Composant2.D13/SCK
  N6: NRF24L1_Emetteur_2_4Ghz.MISO, Composant2.D12/MISO
  N7: R1.Pin_1, Composant2.5V
  N8: Température_extérieur.DQ, Composant2.D7

custom parts:
  NRF24L01: NRF24L01 module
